# Fritzing sketch Diagrama MPU6050 (saved by Fritzing 0.9.3b)
breadboards: 1

parts:
  GY1 = MPU-6050 Board GY-521 [form="♀ (female)" package=THT]
  Componente1 = Arduino Nano (Rev3.0)

nets:
  N1: GY1.pin1, Componente1.5V
  N2: GY1.pin2, GY1.pin7, Componente1.GND
  N3: GY1.pin3, Componente1.A5
  N4: GY1.pin4, Componente1.A4
  N5: GY1.pin8, Componente1.D2

custom parts:
  MPU-6050 Board GY-521: Acelerometro y Giroscopio MPU-6050 Board GY-521
